// Logisim project ALU-Selector.circ as structural Verilog: 3 circuits, main circuit ALU-Operation-Selector
module ALU_Operation_Selector (
  input  add,
  input  sub,
  input  slt,
  input  sltu,
  input  \and ,
  input  \or ,
  input  \nor ,
  input  \xor ,
  input  mult,
  input  mulu,
  input  div,
  input  divu,
  output [3:0] ALU_Selector
);

  Priority_Encoder #(.select(4), .disabled(0)) priority_encoder_1 (
    .in0(add), .in1(sub), .in2(slt), .in3(sltu), .in4(\and ), .in5(\or ), .in6(\nor ), .in7(\xor ),
    .in8(mult), .in9(mulu), .in10(div), .in11(divu), .out(ALU_Selector));  // open: in12, in13, in14, in15, gs, en_out, en_in

  // Notes on the sheet:
  //   ALU Operations
endmodule

module ALU_Input_Selector (
  input  Type_I
);

  Priority_Encoder #(.select(2)) priority_encoder_1 ();  // open: in0, in1, in2, in3, out, gs, en_out, en_in
endmodule

module Const_Extender_Selector (
  input  andi,
  input  ori,
  input  xori,
  output Selector
);

  or or_1 (Selector, andi, ori, xori);
endmodule
