// Logisim project Branch Control.circ as structural Verilog: 1 circuit, main circuit Branch-Control
module Branch_Control (
  input  [31:0] in_1,
  input  [31:0] in_2,
  input  [31:0] in_3,
  input  [25:0] in_4,
  input  [1:0] in_5,
  input  [15:0] in_6,
  input  [2:0] in_7,
  output [31:0] PC_prime
);

  wire comparator_2_eq, multiplexer_1_out, Rs_0, Rs_0_t, Rs__0, Rs__Rt, Rs__Rt_t;
  wire [13:0] bit_extender_1_out;
  wire [31:0] multiplexer_2_out, PC_4, PC_4_x;

  Adder #(.width(32)) adder_1 (.a(in_3), .b(32'h4), .out(PC_4));  // open: cin, cout
  assign bit_extender_1_out = {{13{in_6[15]}}, in_6[15]};  // Bit_Extender bit_extender_1
  Adder #(.width(32)) adder_2 (.a(PC_4), .b({bit_extender_1_out, in_6, 2'b00}), .out(PC_4_x));  // open: cin, cout
  Comparator #(.width(32)) comparator_1 (.a(in_1), .b(in_2), .eq(Rs__Rt_t));  // open: gt, lt
  Comparator #(.width(32)) comparator_2 (.a(in_1), .b({32{1'b0}}), .gt(Rs_0_t), .eq(comparator_2_eq), .lt(Rs_0));
  not not_1 (Rs__Rt, Rs__Rt_t);
  or or_1 (Rs__0, comparator_2_eq, Rs_0);
  Multiplexer #(.select(3), .enable("false")) multiplexer_1 (
    .in0(Rs__Rt_t), .in1(Rs__Rt), .in2(Rs_0_t), .in3(Rs__0), .in4(Rs_0), .out(multiplexer_1_out), .sel(in_7));  // open: in5, in6, in7
  Multiplexer #(.width(32), .enable("false")) multiplexer_2 (
    .in0(PC_4), .in1(PC_4_x), .out(multiplexer_2_out), .sel(multiplexer_1_out));
  Multiplexer #(.select(2), .width(32), .enable("false")) multiplexer_3 (
    .in0(multiplexer_2_out), .in1(multiplexer_2_out), .in2({in_3[31:28], in_4, 2'b00}), .in3(in_1),
    .out(PC_prime), .sel(in_5));

  // Other names for the same wires on the sheet: offset[15:0] = in_6; FlagCondition[2:0] = in_7; dest[25:0] = in_4;
  //   jmp[31:2] = {in_3[31:28], in_4}; PC[31:0] = in_3; Rs[31:0] = in_1; Rt[31:0] = in_2; Selector[1:0] = in_5

  // Notes on the sheet:
  //   Branch Control
endmodule
