// Logisim project Branch-Control-Selector.circ as structural Verilog: 1 circuit, main circuit Branch-Control-Selector
module Branch_Control_Selector (
  input  in_1,
  input  in_2,
  input  in_3,
  input  in_4,
  input  in_5,
  input  in_6,
  input  in_7,
  output [6:0] Selector
);


  assign Selector = {in_7, in_6, in_5, in_4, in_3, in_2, in_1};

  // Other names for the same wires on the sheet: beq = in_1; bne = in_2; blez = in_3; bgtz = in_4; bltz = in_5;
  //   jr = in_6; j = in_7
endmodule
